# Fritzing sketch arduheater (saved by Fritzing 0.9.3b)
perfboards: 1

parts:
  Q3 = npn-Powertransistor [package="TO220 [THT]"]
  Q2 = npn-Powertransistor [package="TO220 [THT]"]
  Q1 = npn-Powertransistor [package="TO220 [THT]"]
  GND = male pin header, 1 pin [form="♂ (male)"]
  UC1 = Arduino Nano (Rev3.0)  # not connected
  NTC+ = male pin header, 4 pins [form="♂ (male)"]
  NTC- = male pin header, 4 pins [form="♂ (male)"]
  NTC~ = male pin header, 4 pins [form="♂ (male)"]
  AREF = male pin header, 1 pin [form="♂ (male)"]
  RST = male pin header, 1 pin [form="♂ (male)"]
  VIN = male pin header, 1 pin [form="♂ (male)"]
  5V = male pin header, 1 pin [form="♂ (male)"]
  D2 = male pin header, 1 pin [form="♂ (male)"]
  R14 = Resistor [tolerance=±1% resistance=10k package=THT]
  R13 = Resistor [tolerance=±1% resistance=10k package=THT]
  R5 = Resistor [tolerance=±1% resistance=10k package=THT]
  R6 = Resistor [tolerance=±1% resistance=10k package=THT]
  R15 = Resistor [tolerance=±5% resistance=10k package=THT]
  PWR2 = male pin header, 1 pin [form="♂ (male)"]
  PWR1 = male pin header, 1 pin [form="♂ (male)"]
  DHT22 = male pin header, 3 pins [form="♂ (male)"]
  PWRIN = Camdenboss CTB0158-2 [part_number=CTB0158-2 package=THT]
  OUT1 = Camdenboss CTB0158-2 [part_number=CTB0158-2 package=THT]
  OUT2 = Camdenboss CTB0158-2 [part_number=CTB0158-2 package=THT]
  OUT3 = Camdenboss CTB0158-2 [part_number=CTB0158-2 package=THT]
  OUT4 = Camdenboss CTB0158-2 [part_number=CTB0158-2 package=THT]
  C1 = Electrolytic Capacitor [capacitance=10µF voltage=20V package="100 mil [THT, electrolytic]"]
  Q4 = npn-Powertransistor [package="TO220 [THT]"]
  PWR3 = male pin header, 1 pin [form="♂ (male)"]
  PWR4 = male pin header, 1 pin [form="♂ (male)"]
  R1 = Resistor [tolerance=±1% resistance=442 package=THT]
  R2 = Resistor [tolerance=±1% resistance=442 package=THT]
  R4 = Resistor [tolerance=±1% resistance=442 package=THT]
  F1 = Resettable Fuse PTC [package=ptc]
  R3 = Resistor [tolerance=±1% resistance=442 package=THT]
  PIN0 = male pin header, 2 pins [form="♂ (male)"]  # not connected
  PIN1 = male pin header, 2 pins [form="♂ (male)"]  # not connected
  PIN2 = male pin header, 1 pin [form="♂ (male)"]  # not connected
  PIN3 = male pin header, 5 pins [form="♂ (male)"]  # not connected
  PIN4 = male pin header, 4 pins [form="♂ (male)"]  # not connected
  D3 = Diode [part_number=1N4007 package=diode-1n4001]

nets:
  N1: Q3.base, R3.Pin_1
  N2: Q3.collector, OUT3.pin2
  GND: Q3.emitter, Q2.emitter, Q1.emitter, GND.pin1, NTC-.pin1, NTC-.pin2, NTC-.pin3, NTC-.pin4, DHT22.pin3, PWRIN.pin1, C1.-, Q4.emitter
  N3: Q2.base, R2.Pin_1
  N4: Q2.collector, OUT2.pin2
  N5: Q1.base, R1.Pin_1
  N6: Q1.collector, OUT1.pin2
  N7: NTC+.pin1, NTC~.pin1, R5.Pin_1
  N8: NTC+.pin2, NTC~.pin2, R6.Pin_1
  N9: NTC+.pin3, NTC~.pin3, R13.Pin_1
  N10: NTC+.pin4, NTC~.pin4, R14.Pin_1
  N11: AREF.pin1, R14.Pin_0, R13.Pin_0, R5.Pin_0, R6.Pin_0
  N12: RST.pin1, C1.+
  N13: VIN.pin1, D3.C
  5V: 5V.pin1, R15.Pin_0, DHT22.pin2
  N14: D2.pin1, R15.Pin_1, DHT22.pin1
  N15: PWR2.pin1, R2.Pin_0
  N16: PWR1.pin1, R1.Pin_0
  N17: PWRIN.pin2, F1.2, D3.A
  12V: OUT1.pin1, OUT2.pin1, OUT3.pin1, OUT4.pin1, F1.1
  N18: OUT4.pin2, Q4.collector
  N19: Q4.base, R4.Pin_1
  N20: PWR3.pin1, R3.Pin_0
  N21: PWR4.pin1, R4.Pin_0

notes:
  PWR1
  PWR3
  PWR2
  PWR4
  12V GND RST 5V D2
  GND
  NTC+
  AREF A3-A0
  OUT4
  OUT3
  OUT2
  OUT1
  4      3      2      1
  DATA VCC GND
  PWR IN
